# Fritzing sketch 7segment (saved by Fritzing 0.9.2b)
breadboards: 1

parts:
  Q1 = NPN-Transistor [package="TO92 [THT]"]
  R1 = Resistor [tolerance=±5% resistance=220 package=THT]
  R2 = Resistor [tolerance=±5% resistance=220 package=THT]
  7_Segment1 = 7 Segment Display
  C1 = Starter AVR Board

nets:
  N1: Q1.E, R1.Pin_0
  N2: Q1.B, R2.Pin_1
  N3: Q1.C, 7_Segment1.common_anode
  N4: R1.Pin_1, C1.+5V
  N5: R2.Pin_0, C1.PD0
  N6: 7_Segment1.Segment_E, C1.PB4
  N7: 7_Segment1.Segment_D, C1.PB3
  N8: 7_Segment1.Segment_C, C1.PB2
  N9: 7_Segment1.Segment_DP, C1.PB7
  N10: 7_Segment1.Segment_B, C1.PB1
  N11: 7_Segment1.Segment_A, C1.PB0
  N12: 7_Segment1.Segment_F, C1.PB5
  N13: 7_Segment1.Segment_G, C1.PB6

custom parts:
  Starter AVR Board: ATmega 32 Starter Board
