# Fritzing sketch GLCD (saved by Fritzing 0.9.2b)

parts:
  C1 = Starter AVR Board
  Breakout1 = LCD breakout [package="DIP (Dual Inline) [THT]"]
  GLCD_128x1 = 128 x 64 Graphic LCD  # not connected

nets:
  N1: C1.PA7, Breakout1.pin_11
  N2: C1.PA6, Breakout1.pin_10
  N3: C1.PA5, Breakout1.pin_9
  N4: C1.PA4, Breakout1.pin8
  N5: C1.PA3, Breakout1.pin7
  N6: C1.PA2, Breakout1.pin6
  N7: C1.PA1, Breakout1.pin5
  N8: C1.PA0, Breakout1.pin4
  N9: C1.PC4, Breakout1.pin_13
  N10: C1.PC3, Breakout1.pin_12
  N11: C1.PC2, Breakout1.pin3
  N12: C1.PC1, Breakout1.pin2
  N13: C1.PC0, Breakout1.pin1
  N14: C1.GND, Breakout1.pin_14
  N15: C1.+5V, Breakout1.pin_15

custom parts:
  Starter AVR Board: ATmega 32 Starter Board
