# Fritzing sketch LM35 (saved by Fritzing 0.9.2b)
breadboards: 1

parts:
  C1 = Starter AVR Board
  T1 = LM35 Temperature Sensor [package="TO92 [THT]"]

nets:
  N1: C1.PA1, T1.Vout
  VIN: C1.VIN, T1.GND
  N2: C1.+5V, T1.+Vs

custom parts:
  Starter AVR Board: ATmega 32 Starter Board
