# Fritzing sketch RTC (saved by Fritzing 0.9.2b)

parts:
  C1 = Starter AVR Board
  C2 = EEPROM & RTC breakout
  LCD1 = LCD screen  # not connected

nets:
  N1: C1.PC1, C2.SDA
  N2: C1.PC0, C2.SCL
  GND: C1.GND, C2.GND
  +5V: C1.+5V, C2.5V

custom parts:
  Starter AVR Board: ATmega 32 Starter Board
