# Fritzing sketch Stepper (saved by Fritzing 0.9.2b)
breadboards: 1

parts:
  C1 = Starter AVR Board
  MD09B1 = A4988 Stepper Motor Driver Carrier
  M1 = Stepper Motor - Bipolar  # not connected
  Power_plug1 = Power plug

nets:
  N1: C1.PD5, MD09B1.Enable
  N2: C1.PD6, MD09B1.DIR
  N3: C1.PD7, MD09B1.STEP
  N4: C1.GND, MD09B1.GROUND#147
  +5V: C1.+5V, MD09B1.VDD
  N5: MD09B1.RESET, MD09B1.SLEEP
  N6: MD09B1.VMOT, Power_plug1.VCC
  N7: MD09B1.GROUND#141, Power_plug1.GND

custom parts:
  Starter AVR Board: ATmega 32 Starter Board
  A4988 Stepper Motor Driver Carrier: The Pololu stepper motor driver carrier for the A4988 motor driver integrated circuits. http://www.pololu.com/catalog/product/1182
  Stepper Motor - Bipolar: Simple, but very powerful bi polar stepper motor. 4 wire
