# Fritzing sketch Ultrasonic (saved by Fritzing 0.9.2b)

parts:
  Part1 = SRF05 Ultrasonic Rangefinder
  C1 = Starter AVR Board

nets:
  VCC: Part1.VCC, C1.+5V
  N1: Part1.Trig, C1.PB3
  N2: Part1.Echo, C1.PD3
  GND: Part1.GND, C1.GND

custom parts:
  Starter AVR Board: ATmega 32 Starter Board
